// Logisim project Milestone.circ as structural Verilog: 5 circuits, main circuit main
// B0
module main (
  output E,
  output [2:0] ALU_sel
);

  wire ADD, AND, and_2_out, and_3_out, and_4_out, and_5_out, and_7_out, and_8_out, and_9_out, and_10_out,
       and_11_out, and_12_out, and_13_out, and_14_out, and_15_out, and_16_out, and_17_out, and_18_out,
       and_19_out, and_20_out, and_21_out, and_22_out, and_23_out, and_24_out, and_25_out, and_26_out,
       and_27_out, and_28_out, and_29_out, and_30_out, and_31_out, and_34_out, and_35_out, B0, B1, B2, B3,
       B4, B5, B6, B7, B8, B9, B10, B11, CLK, CLR_AC, CLR_AR, CLR_DR, CLR_IR, CLR_PC, CLR_SC, CLR_TR, D0, D1,
       D2, D3, D4, D5, D6, D7, I, I_prime_T3D7B2, INC_DR, INC_PC, LD_AC, LD_AR, LD_DR, LD_IR, LD_PC, LD_TR,
       nor_1_out, not_1_out, not_2_out, not_3_out, not_4_out, OR, PC_CLR, r, READ, SUB, T0, T2, T3, T4, T5,
       T6, T7, T8, T9, T10, T11, T12, T13, T14, T15, Transfer_DR, WRITE, XOR;
  wire [2:0] or_5_out;
  wire [6:0] Address_Memory, IN_AR, IN_PC, OUT_PC;
  wire [15:0] bit_extender_1_out, bit_extender_2_out, IN_AC, IN_DR, OUT_AC, OUT_DR, OUT_IR, OUT_Memory,
       OUT_TR;

  assign bit_extender_1_out = {{9{1'b0}}, Address_Memory};  // Bit_Extender bit_extender_1
  assign bit_extender_2_out = {{9{1'b0}}, OUT_PC};  // Bit_Extender bit_extender_2
  D_Flip_Flop u_PC_CLR (.clk(CLK), .D(PC_CLR), .Q(CLR_PC), .en(1'b1));  // open: Qn, preset, reset
  not not_1 (not_1_out, I);
  and u_r (r, D7, not_1_out, T3);
  Multiplexer #(.select(3), .width(16)) multiplexer_1 (
    .in0(OUT_Memory), .in1(bit_extender_1_out), .in2(OUT_TR), .in3(OUT_DR), .in4(OUT_AC),
    .in5(bit_extender_2_out), .in6(OUT_IR), .out(IN_DR), .sel(or_5_out), .en(1'b1));  // open: in7
  and and_1 (I_prime_T3D7B2, B2, r);
  and and_2 (and_2_out, D2, T4);
  and and_3 (and_3_out, D1, T4);
  and and_4 (and_4_out, D5, T4);
  and and_5 (and_5_out, D0, T4);
  and and_6 (WRITE, D3, T4);
  and and_7 (and_7_out, D2, T4);
  and and_8 (and_8_out, D1, T4);
  and and_9 (and_9_out, D5, T4);
  and and_10 (and_10_out, D5, T6);
  and and_11 (and_11_out, B5, r);
  and and_12 (and_12_out, D0, T4);
  Bit_Extender #(.in_width(16), .out_width(7)) bit_extender_3 (.in(IN_DR), .out(IN_AR));
  Bit_Extender #(.in_width(16), .out_width(7)) bit_extender_4 (.in(IN_DR), .out(IN_PC));
  and and_13 (and_13_out, D7, T3);
  and and_14 (and_14_out, D5, T5);
  nor nor_1 (nor_1_out, OUT_AC[0], OUT_AC[1], OUT_AC[2], OUT_AC[3], OUT_AC[4], OUT_AC[5], OUT_AC[6], OUT_AC[7], OUT_AC[8], OUT_AC[9], OUT_AC[10], OUT_AC[11], OUT_AC[12], OUT_AC[13], OUT_AC[14], OUT_AC[15]);
  RAM #(.addrWidth(7), .dataWidth(16), .bus("separate")) ram_1 (
    .addr(Address_Memory), .din(IN_DR), .data(OUT_Memory), .str(WRITE), .clk(CLK), .ld(READ));  // open: sel, clr
  and and_15 (and_15_out, D3, T4);
  or or_1 (READ, and_2_out, and_3_out, LD_IR, and_4_out, and_5_out);
  or or_2 (LD_DR, and_7_out, and_8_out, and_9_out, and_10_out, and_11_out, and_12_out);
  or or_3 (or_5_out[1], T2, and_16_out);
  or or_4 (or_5_out[2], and_14_out, and_13_out, T2, and_15_out, T0);
  ALU ALU (.A(OUT_DR), .B(OUT_AC), .ALU_selection(ALU_sel), .E(E), .Result(IN_AC));
  or or_5 (or_5_out[0], T0, and_18_out);
  and and_16 (and_16_out, D5, T6);
  and and_17 (and_17_out, nor_1_out, I_prime_T3D7B2);
  Register #(.width(16)) DR (.D(IN_DR), .en(LD_DR), .Q(OUT_DR), .clk(CLK), .clr(CLR_DR));
  and and_18 (and_18_out, D4, T4);
  or or_6 (INC_PC, and_17_out, LD_IR);
  not not_2 (not_2_out, I);
  Clock u_CLK (.out(CLK));
  and and_19 (and_19_out, D2, T5);
  and and_20 (and_20_out, D1, T5);
  and and_21 (and_21_out, D5, T5);
  and and_22 (and_22_out, D5, T7);
  and and_23 (and_23_out, D7, B5, not_2_out, T4);
  and and_24 (and_24_out, D0, T5);
  Register #(.width(7)) AR (.D(IN_AR), .en(LD_AR), .Q(Address_Memory), .clk(CLK), .clr(CLR_AR));
  CU cu_1 (
    .IR(OUT_IR), .CLR_SC(CLR_SC), .IR_0_11({B11, B10, B9, B8, B7, B6, B5, B4, B3, B2, B1, B0}), .D0(D0),
    .D1(D1), .D2(D2), .D3(D3), .D4(D4), .D5(D5), .D6(D6), .D7(D7), .T0(T0), .T1(LD_IR), .T2(T2), .T3(T3),
    .T4(T4), .T5(T5), .T6(T6), .T7(T7), .T8(T8), .T9(T9), .T10(T10), .T11(T11), .T12(T12), .T13(T13),
    .T14(T14), .T15(T15), .I(I));
  or or_7 (LD_AC, and_19_out, and_20_out, and_21_out, and_22_out, and_23_out, and_24_out);
  not not_3 (not_3_out, I);
  Register #(.width(16)) TR (.D(IN_DR), .en(LD_TR), .Q(OUT_TR), .clk(CLK), .clr(CLR_TR));
  Priority_Encoder priority_encoder_1 (
    .in1(ADD), .in2(SUB), .in3(Transfer_DR), .in4(AND), .in5(OR), .in6(XOR), .in7(INC_DR), .out(ALU_sel));  // open: in0, en_in, gs, en_out
  and and_25 (and_25_out, D2, T5);
  and and_26 (and_26_out, D1, T5);
  and and_27 (and_27_out, D5, T7);
  and and_28 (and_28_out, D4, T4);
  and and_29 (and_29_out, D7, B5, not_3_out, T4);
  and and_30 (and_30_out, D0, T5);
  and and_31 (and_31_out, D3, T4);
  Register #(.width(16)) AC (.D(IN_AC), .en(LD_AC), .Q(OUT_AC), .clk(CLK), .clr(CLR_AC));
  and and_32 (LD_PC, D4, T4);
  or or_8 (CLR_SC, and_25_out, and_26_out, and_27_out, I_prime_T3D7B2, and_28_out, and_29_out, and_30_out, and_31_out);
  or or_9 (LD_AR, T0, T2);
  and and_33 (LD_TR, D5, T5);
  Register #(.width(16)) IR (.D(IN_DR), .en(LD_IR), .Q(OUT_IR), .clk(CLK), .clr(CLR_IR));
  not not_4 (not_4_out, I);
  Counter #(.width(7), .max('h7f)) PC (
    .load(LD_PC), .D(IN_PC), .count(INC_PC), .Q(OUT_PC), .clk(CLK), .clr(CLR_PC));  // open: carry
  and u_ADD (ADD, D1, T5);
  and u_SUB (SUB, D5, T7);
  and and_34 (and_34_out, D2, T5);
  and and_35 (and_35_out, D5, T5);
  and AND_36 (AND, D0, T5);
  and INC (INC_DR, D7, not_4_out, B5, T4);
  or or_10 (Transfer_DR, and_34_out, and_35_out);

  // Other names for the same wires on the sheet: IN_IR[15:0] = IN_DR; IN_Memory[15:0] = IN_DR; IN_TR[15:0] = IN_DR;
  //   OUT_AR[6:0] = Address_Memory; T1 = LD_IR
endmodule

module ALU (
  input  [15:0] A,
  input  [15:0] B,
  input  [2:0] ALU_selection,
  output E,
  output [15:0] Result
);

  wire [15:0] arithmetic_circuit_1_a_1, arithmetic_circuit_1_a_b, arithmetic_circuit_1_a_b_2, Logic_a_and_b,
       Logic_a_or_b, Logic_a_xor_b;

  Arithmetic_Circuit arithmetic_circuit_1 (
    .A(A), .B(B), .E(E), .A_1(arithmetic_circuit_1_a_1), .A_B(arithmetic_circuit_1_a_b),
    .A_B_2(arithmetic_circuit_1_a_b_2));
  Logic_Circuit Logic (.A(A), .B(B), .A_AND_B(Logic_a_and_b), .A_OR_B(Logic_a_or_b), .A_XOR_B(Logic_a_xor_b));
  Multiplexer #(.select(3), .width(16)) multiplexer_1 (
    .in1(arithmetic_circuit_1_a_b), .in2(arithmetic_circuit_1_a_b_2), .in3(A), .in4(Logic_a_and_b),
    .in5(Logic_a_or_b), .in6(Logic_a_xor_b), .in7(arithmetic_circuit_1_a_1), .out(Result),
    .sel(ALU_selection), .en(1'b1));  // open: in0
endmodule

module Arithmetic_Circuit (
  input  [15:0] A,
  input  [15:0] B,
  output E,
  output [15:0] A_1,
  output [15:0] A_B,
  output [15:0] A_B_2
);

  wire adder_1_cout, adder_2_cout, subtractor_1_bout;

  Adder #(.width(16)) adder_1 (.a(A), .b(16'h1), .out(A_1), .cin(1'b0), .cout(adder_1_cout));
  Adder #(.width(16)) adder_2 (.a(A), .b(B), .out(A_B), .cin(1'b0), .cout(adder_2_cout));
  Subtractor #(.width(16)) subtractor_1 (.a(A), .b(B), .out(A_B_2), .bin(1'b0), .bout(subtractor_1_bout));
  or or_1 (E, adder_1_cout, adder_2_cout, subtractor_1_bout);
endmodule

module Logic_Circuit (
  input  [15:0] A,
  input  [15:0] B,
  output [15:0] A_AND_B,
  output [15:0] A_OR_B,
  output [15:0] A_XOR_B
);

  assign A_AND_B = A & B;  // AND_Gate and_1, 16 bits wide
  assign A_OR_B = A | B;  // OR_Gate or_1, 16 bits wide
  assign A_XOR_B = A ^ B;  // XOR_Gate xor_1, 16 bits wide
endmodule

module CU (
  input  [15:0] IR,
  input  CLR_SC,
  output [11:0] IR_0_11,
  output D0,
  output D1,
  output D2,
  output D3,
  output D4,
  output D5,
  output D6,
  output D7,
  output T0,
  output T1,
  output T2,
  output T3,
  output T4,
  output T5,
  output T6,
  output T7,
  output T8,
  output T9,
  output T10,
  output T11,
  output T12,
  output T13,
  output T14,
  output T15,
  output I
);

  wire CLK, not_1_out, SC_CLR_q;
  wire [3:0] SC_q;

  Clock clock_1 (.out(CLK));
  not not_1 (not_1_out, CLR_SC);
  Decoder #(.select(3)) decoder_1 (
    .out0(D0), .out1(D1), .out2(D2), .out3(D3), .out4(D4), .out5(D5), .out6(D6), .out7(D7), .sel(IR[14:12]),
    .en(1'b1));
  Counter #(.width(4), .max('hf)) SC (.count(not_1_out), .Q(SC_q), .clk(CLK), .clr(SC_CLR_q));  // open: load, D, carry
  D_Flip_Flop SC_CLR (.clk(CLK), .D(CLR_SC), .Q(SC_CLR_q), .en(1'b1));  // open: Qn, preset, reset
  Decoder #(.select(4)) decoder_2 (
    .out0(T0), .out1(T1), .out2(T2), .out3(T3), .out4(T4), .out5(T5), .out6(T6), .out7(T7), .out8(T8),
    .out9(T9), .out10(T10), .out11(T11), .out12(T12), .out13(T13), .out14(T14), .out15(T15), .sel(SC_q),
    .en(1'b1));
  D_Flip_Flop d_ff_1 (.clk(CLK), .D(IR[15]), .Q(I), .en(1'b1));  // open: Qn, preset, reset

  assign IR_0_11 = IR[11:0];
endmodule
